// Logisim project 16x1.circ as structural Verilog: 2 circuits, main circuit main
module main (
  input  B4,
  input  B3,
  input  A15,
  input  A7,
  input  B2,
  input  A11,
  input  A3,
  input  A13,
  input  B1,
  input  A5,
  input  A9,
  input  A1,
  input  A14,
  input  A6,
  input  A10,
  input  A2,
  input  A12,
  input  A4,
  input  A8,
  input  A0,
  output out_21
);

  wire doisxum_1_o, doisxum_2_o, doisxum_3_o, doisxum_4_o, doisxum_5_o, doisxum_6_o, doisxum_7_o,
       doisxum_8_o, doisxum_9_o, doisxum_10_o, doisxum_11_o, doisxum_12_o, doisxum_13_o, doisxum_14_o;

  doisxum doisxum_1 (.A1(A15), .S(B4), .A2(A7), .O(doisxum_1_o));
  doisxum doisxum_2 (.A1(A11), .S(B4), .A2(A3), .O(doisxum_2_o));
  doisxum doisxum_3 (.A1(A13), .S(B4), .A2(A5), .O(doisxum_3_o));
  doisxum doisxum_4 (.A1(A9), .S(B4), .A2(A1), .O(doisxum_4_o));
  doisxum doisxum_5 (.A1(A14), .S(B4), .A2(A6), .O(doisxum_5_o));
  doisxum doisxum_6 (.A1(A10), .S(B4), .A2(A2), .O(doisxum_6_o));
  doisxum doisxum_7 (.A1(A12), .S(B4), .A2(A4), .O(doisxum_7_o));
  doisxum doisxum_8 (.A1(A8), .S(B4), .A2(A0), .O(doisxum_8_o));
  doisxum doisxum_9 (.A1(doisxum_1_o), .S(B3), .A2(doisxum_2_o), .O(doisxum_9_o));
  doisxum doisxum_10 (.A1(doisxum_3_o), .S(B3), .A2(doisxum_4_o), .O(doisxum_10_o));
  doisxum doisxum_11 (.A1(doisxum_5_o), .S(B3), .A2(doisxum_6_o), .O(doisxum_11_o));
  doisxum doisxum_12 (.A1(doisxum_7_o), .S(B3), .A2(doisxum_8_o), .O(doisxum_12_o));
  doisxum doisxum_13 (.A1(doisxum_9_o), .S(B2), .A2(doisxum_10_o), .O(doisxum_13_o));
  doisxum doisxum_14 (.A1(doisxum_11_o), .S(B2), .A2(doisxum_12_o), .O(doisxum_14_o));
  doisxum doisxum_15 (.A1(doisxum_13_o), .S(B1), .A2(doisxum_14_o), .O(out_21));
endmodule

module doisxum (
  input  A1,
  input  S,
  input  A2,
  output O
);

  wire and_1_out, and_2_out, not_1_out;

  not not_1 (not_1_out, S);
  and and_1 (and_1_out, A1, S);
  and and_2 (and_2_out, not_1_out, A2);
  or or_1 (O, and_1_out, and_2_out);
endmodule
