// Logisim project demux.circ as structural Verilog
module umxquatro (
  input  S1,
  input  S0,
  input  E,
  output O0,
  output O1,
  output O2,
  output O3
);

  wire umdois_1_o0, umdois_1_o1;

  umdois umdois_1 (.S(S0), .E(E), .O0(umdois_1_o0), .O1(umdois_1_o1));
  umdois umdois_2 (.S(S1), .E(umdois_1_o0), .O0(O0), .O1(O1));
  umdois umdois_3 (.S(S1), .E(umdois_1_o1), .O0(O2), .O1(O3));
endmodule

module umoito (
  input  in_1,
  input  in_2,
  input  in_3,
  input  in_4,
  output out_5,
  output out_6,
  output out_7,
  output out_8,
  output out_9,
  output out_10,
  output out_11,
  output out_12
);

  wire umdois_1_o0, umdois_1_o1, umdois_2_o0, umdois_2_o1, umdois_3_o0, umdois_3_o1;

  umdois umdois_1 (.S(in_3), .E(in_4), .O0(umdois_1_o0), .O1(umdois_1_o1));
  umdois umdois_2 (.S(in_2), .E(umdois_1_o0), .O0(umdois_2_o0), .O1(umdois_2_o1));
  umdois umdois_3 (.S(in_2), .E(umdois_1_o1), .O0(umdois_3_o0), .O1(umdois_3_o1));
  umdois umdois_4 (.S(in_1), .E(umdois_2_o0), .O0(out_5), .O1(out_6));
  umdois umdois_5 (.S(in_1), .E(umdois_2_o1), .O0(out_7), .O1(out_8));
  umdois umdois_6 (.S(in_1), .E(umdois_3_o0), .O0(out_9), .O1(out_10));
  umdois umdois_7 (.S(in_1), .E(umdois_3_o1), .O0(out_11), .O1(out_12));
endmodule

module umdois (
  input  S,
  input  E,
  output O0,
  output O1
);

  and and_1 (O0, ~S, E);  // AND_Gate
  and and_2 (O1, S, E);
endmodule
