// Logisim project mux.circ as structural Verilog: 3 circuits, main circuit main
module main (
  input  A,
  input  B,
  input  S1,
  input  S0,
  input  C,
  input  D,
  output O
);

  wire halfmux_1_o, halfmux_2_o;

  halfmux halfmux_1 (.A0(A), .S(S0), .A1(B), .O(halfmux_1_o));
  halfmux halfmux_2 (.A0(C), .S(S0), .A1(D), .O(halfmux_2_o));
  halfmux halfmux_3 (.A0(halfmux_1_o), .S(S1), .A1(halfmux_2_o), .O(O));
endmodule

module halfmux (
  input  A0,
  input  S,
  input  A1,
  output O
);

  wire and_1_out, and_2_out, not_1_out;

  not not_1 (not_1_out, S);
  and and_1 (and_1_out, A0, not_1_out);
  and and_2 (and_2_out, S, A1);
  or or_1 (O, and_1_out, and_2_out);
endmodule

module oito (
  input  A0,
  input  A2,
  input  S1,
  input  A1,
  input  A12,
  input  S3,
  input  A3,
  input  A23,
  input  S2,
  input  A13,
  input  A123,
  output O
);

  wire main_1_o, main_2_o;

  main main_1 (.A(A0), .B(A2), .S1(S1), .S0(S2), .C(A1), .D(A12), .O(main_1_o));
  main main_2 (.A(A3), .B(A23), .S1(S1), .S0(S2), .C(A13), .D(A123), .O(main_2_o));
  main main_3 (.A(main_1_o), .B(main_1_o), .S1(S3), .S0(S3), .C(main_2_o), .D(main_2_o), .O(O));
endmodule
