// Logisim project somador.circ as structural Verilog: 3 circuits, main circuit main
module main (
  input  in_1,
  input  in_2,
  input  in_3,
  input  in_4,
  input  in_5,
  input  in_6,
  output out_7,
  output out_8,
  output out_9,
  output out_10
);

  wire fulladder_1_co, halfadder_1_co;

  halfadder halfadder_1 (.B1(in_1), .B2(in_2), .S(out_8), .Co(halfadder_1_co));
  fulladder fulladder_1 (.Ci(halfadder_1_co), .B1(in_3), .B2(in_5), .S(out_7), .Co(fulladder_1_co));
  fulladder fulladder_2 (.Ci(fulladder_1_co), .B1(in_4), .B2(in_6), .S(out_9), .Co(out_10));
endmodule

module halfadder (
  input  B1,
  input  B2,
  output S,
  output Co
);

  xor xor_1 (S, B1, B2);
  and and_1 (Co, B1, B2);
endmodule

module fulladder (
  input  Ci,
  input  B1,
  input  B2,
  output S,
  output Co
);

  wire and_1_out, and_2_out, and_3_out, xor_1_out;

  xor xor_1 (xor_1_out, B1, B2);
  and and_1 (and_1_out, B1, B2);
  and and_2 (and_2_out, B1, Ci);
  and and_3 (and_3_out, B2, Ci);
  xor xor_2 (S, Ci, xor_1_out);
  or or_1 (Co, and_1_out, and_2_out, and_3_out);
endmodule
