// Logisim project trabalhofinal.circ as structural Verilog: 7 circuits, main circuit main
module main (
);

  wire and_1_out, and_2_out, and_3_out, Barco1_p1, Barco1_p2, Barco1_p3, Barco1_p4, Barco2_sw1, Barco2_sw2,
       Barco2_sw3, Barco2_sw4, comparador_1_acerto, comparador_2_acerto, decodificador_1_b1,
       decodificador_1_b2, decodificador_1_b3, decodificador_1_b4, Disparo_out, or_1_out, Tabuleiro_p1,
       Tabuleiro_p2, Tabuleiro_p3, Tabuleiro_p4;

  // DipSwitch #(.number(4)) Tabuleiro: pin names not known; wires that end beside it: Tabuleiro_p1, Tabuleiro_p2, Tabuleiro_p3, Tabuleiro_p4
  // DipSwitch #(.number(4)) Barco1: pin names not known; wires that end beside it: Barco1_p1, Barco1_p2, Barco1_p3, Barco1_p4
  DipSwitch #(.number(4)) Barco2 (.sw1(Barco2_sw1), .sw2(Barco2_sw2), .sw3(Barco2_sw3), .sw4(Barco2_sw4));
  Decodificador decodificador_1 (
    .A(Tabuleiro_p1), .B(Tabuleiro_p2), .C(Tabuleiro_p3), .D(Tabuleiro_p4), .B1(decodificador_1_b1),
    .B2(decodificador_1_b2), .B3(decodificador_1_b3), .B4(decodificador_1_b4));
  Comparador comparador_1 (
    .A(decodificador_1_b1), .B1A(Barco1_p1), .B(decodificador_1_b2), .B1B(Barco1_p2), .C(decodificador_1_b3),
    .B1C(Barco1_p3), .D(decodificador_1_b4), .B1D(Barco1_p4), .Acerto(comparador_1_acerto));
  Comparador comparador_2 (
    .A(decodificador_1_b1), .B1A(Barco2_sw1), .B(decodificador_1_b2), .B1B(Barco2_sw2),
    .C(decodificador_1_b3), .B1C(Barco2_sw3), .D(decodificador_1_b4), .B1D(Barco2_sw4),
    .Acerto(comparador_2_acerto));
  Button Disparo (.out(Disparo_out));
  and and_1 (and_1_out, ~comparador_1_acerto, ~comparador_2_acerto);  // AND_Gate
  or or_1 (or_1_out, comparador_1_acerto, comparador_2_acerto);
  and and_2 (and_2_out, Disparo_out, and_1_out);
  and and_3 (and_3_out, Disparo_out, or_1_out);
  LED led_1 (.in(and_2_out));
  LED led_2 (.in(and_3_out));
endmodule

module S1 (
  input  A,
  input  B,
  input  C,
  input  D,
  output B1
);

  wire and_1_out, and_2_out, and_3_out, and_4_out;

  and and_1 (and_1_out, ~A, ~B);  // AND_Gate
  and and_2 (and_2_out, ~A, D);  // AND_Gate
  and and_3 (and_3_out, B, C, D);
  and and_4 (and_4_out, A, B, ~C, ~D);  // AND_Gate
  or or_1 (B1, and_1_out, and_2_out, and_3_out, and_4_out);
endmodule

module Decodificador (
  input  A,
  input  B,
  input  C,
  input  D,
  output B1,
  output B2,
  output B3,
  output B4
);

  S1 s1_1 (.A(A), .B(B), .C(C), .D(D), .B1(B1));
  S2 s2_1 (.A(A), .B(B), .C(C), .D(D), .B2(B2));
  S3 s3_1 (.A(A), .B(B), .C(C), .D(D), .B3(B3));
  S4 s4_1 (.A(A), .B(B), .C(C), .D(D), .B4(B4));
endmodule

module S2 (
  input  A,
  input  B,
  input  C,
  input  D,
  output B2
);

  wire and_1_out, and_2_out, and_3_out, and_4_out, and_5_out;

  and and_1 (and_1_out, ~A, ~C, ~D);  // AND_Gate
  and and_2 (and_2_out, ~B, ~C, D);  // AND_Gate
  and and_3 (and_3_out, A, ~B, C);  // AND_Gate
  and and_4 (and_4_out, ~B, C, ~D);  // AND_Gate
  and and_5 (and_5_out, ~A, B, C, D);  // AND_Gate
  or or_1 (B2, and_1_out, and_2_out, and_3_out, and_4_out, and_5_out);
endmodule

module S3 (
  input  A,
  input  B,
  input  C,
  input  D,
  output B3
);

  wire and_1_out, and_2_out, and_3_out, and_4_out, and_5_out;

  and and_1 (and_1_out, ~A, ~C, D);  // AND_Gate
  and and_2 (and_2_out, A, B, ~D);  // AND_Gate
  and and_3 (and_3_out, A, ~B, D);  // AND_Gate
  and and_4 (and_4_out, A, ~B, ~C);  // AND_Gate
  and and_5 (and_5_out, ~A, ~B, C, ~D);  // AND_Gate
  or or_1 (B3, and_1_out, and_2_out, and_3_out, and_4_out, and_5_out);
endmodule

module S4 (
  input  A,
  input  B,
  input  C,
  input  D,
  output B4
);

  wire and_1_out, and_2_out, and_3_out;

  and and_1 (and_1_out, ~A, ~C);  // AND_Gate
  and and_2 (and_2_out, ~B, ~C);  // AND_Gate
  and and_3 (and_3_out, A, B, D);
  or or_1 (B4, and_1_out, and_2_out, and_3_out);
endmodule

module Comparador (
  input  A,
  input  B1A,
  input  B,
  input  B1B,
  input  C,
  input  B1C,
  input  D,
  input  B1D,
  output Acerto
);

  wire xnor_1_out, xnor_2_out, xnor_3_out, xnor_4_out;

  xnor xnor_1 (xnor_1_out, A, B1A);
  xnor xnor_2 (xnor_2_out, B, B1B);
  xnor xnor_3 (xnor_3_out, C, B1C);
  xnor xnor_4 (xnor_4_out, D, B1D);
  and and_1 (Acerto, xnor_1_out, xnor_2_out, xnor_3_out, xnor_4_out);
endmodule
