// Digital circuit contador mod doze assinc.dig as structural Verilog
module contador_mod_doze_assinc (
  input  clk
);

  wire jk_ff_as_1_nq, jk_ff_as_1_q, jk_ff_as_2_nq, jk_ff_as_2_q, jk_ff_as_3_nq, jk_ff_as_3_q, jk_ff_as_4_nq,
       jk_ff_as_4_q, nand_1_out;

  JK_FF_AS jk_ff_as_1 (
    .Set(1'b0), .J(1'b1), .C(~clk), .K(1'b1), .Clr(~nand_1_out), .Q(jk_ff_as_1_q), .nQ(jk_ff_as_1_nq));
  JK_FF_AS jk_ff_as_2 (
    .Set(1'b0), .J(1'b1), .C(~jk_ff_as_1_q), .K(1'b1), .Clr(~nand_1_out), .Q(jk_ff_as_2_q), .nQ(jk_ff_as_2_nq));
  JK_FF_AS jk_ff_as_3 (
    .Set(1'b0), .J(1'b1), .C(~jk_ff_as_2_q), .K(1'b1), .Clr(~nand_1_out), .Q(jk_ff_as_3_q), .nQ(jk_ff_as_3_nq));
  LED led_1 (.in(jk_ff_as_4_q));
  JK_FF_AS jk_ff_as_4 (
    .Set(1'b0), .J(1'b1), .C(~jk_ff_as_3_q), .K(1'b1), .Clr(~nand_1_out), .Q(jk_ff_as_4_q), .nQ(jk_ff_as_4_nq));
  LED led_2 (.in(jk_ff_as_3_q));
  LED led_3 (.in(jk_ff_as_2_q));
  nand nand_1 (nand_1_out, jk_ff_as_3_q, jk_ff_as_4_q);
  LED led_4 (.in(jk_ff_as_1_q));
endmodule
