// Digital circuit registrador 4 bits paralelo.dig as structural Verilog
module registrador_4_bits_paralelo (
  input  in_1,
  input  in_2,
  input  in_3,
  input  in_4,
  input  clk
);

  wire d_ff_1_q, d_ff_2_q, d_ff_3_q, d_ff_4_q;

  D_FF d_ff_1 (.D(in_1), .C(clk), .Q(d_ff_1_q));  // open: nQ
  LED led_1 (.in(d_ff_1_q));
  D_FF d_ff_2 (.D(in_2), .C(clk), .Q(d_ff_2_q));  // open: nQ
  LED led_2 (.in(d_ff_2_q));
  D_FF d_ff_3 (.D(in_3), .C(clk), .Q(d_ff_3_q));  // open: nQ
  LED led_3 (.in(d_ff_3_q));
  D_FF d_ff_4 (.D(in_4), .C(clk), .Q(d_ff_4_q));  // open: nQ
  LED led_4 (.in(d_ff_4_q));
endmodule
