// Digital circuit trabalho gray.dig as structural Verilog
module trabalho_gray (
  input  clk
);

  wire and_1_out, and_2_out, and_3_out, and_4_out, and_5_out, and_6_out, and_7_out, and_8_out, and_9_out,
       and_10_out, and_11_out, and_12_out, and_13_out, and_14_out, and_15_out, and_16_out, jk_ff_1_q,
       jk_ff_2_q, jk_ff_3_q, jk_ff_4_q, or_1_out, or_2_out, or_3_out, or_4_out;

  and and_1 (and_1_out, jk_ff_2_q, ~jk_ff_3_q, ~jk_ff_4_q);  // And
  and and_2 (and_2_out, ~jk_ff_2_q, ~jk_ff_3_q, ~jk_ff_4_q);  // And
  JK_FF jk_ff_1 (.J(and_1_out), .C(clk), .K(and_2_out), .Q(jk_ff_1_q));  // open: nQ
  and and_3 (and_3_out, jk_ff_1_q, jk_ff_3_q, ~jk_ff_4_q);  // And
  and and_4 (and_4_out, ~jk_ff_1_q, ~jk_ff_2_q, ~jk_ff_3_q);  // And
  and and_5 (and_5_out, ~jk_ff_3_q, jk_ff_2_q, jk_ff_1_q);  // And
  and and_6 (and_6_out, jk_ff_3_q, ~jk_ff_2_q, jk_ff_1_q);  // And
  and and_7 (and_7_out, jk_ff_3_q, jk_ff_2_q, ~jk_ff_1_q);  // And
  and and_8 (and_8_out, ~jk_ff_4_q, jk_ff_3_q, ~jk_ff_1_q);  // And
  JK_FF jk_ff_2 (.J(and_8_out), .C(clk), .K(and_3_out), .Q(jk_ff_2_q));  // open: nQ
  LED led_1 (.in(jk_ff_1_q));
  and and_9 (and_9_out, jk_ff_4_q, ~jk_ff_2_q, jk_ff_1_q);  // And
  LED led_2 (.in(jk_ff_2_q));
  or or_1 (or_1_out, and_4_out, and_5_out, and_6_out, and_7_out);
  and and_10 (and_10_out, ~jk_ff_1_q, jk_ff_2_q, jk_ff_4_q);  // And
  or or_2 (or_2_out, and_10_out, and_9_out);
  LED led_3 (.in(jk_ff_3_q));
  and and_11 (and_11_out, jk_ff_4_q, jk_ff_2_q, jk_ff_1_q);
  LED led_4 (.in(jk_ff_4_q));
  or or_3 (or_3_out, and_12_out, and_11_out);
  JK_FF jk_ff_3 (.J(or_3_out), .C(clk), .K(or_2_out), .Q(jk_ff_3_q));  // open: nQ
  and and_12 (and_12_out, jk_ff_4_q, ~jk_ff_2_q, ~jk_ff_1_q);  // And
  and and_13 (and_13_out, ~jk_ff_3_q, ~jk_ff_2_q, jk_ff_1_q);  // And
  JK_FF jk_ff_4 (.J(or_1_out), .C(clk), .K(or_4_out), .Q(jk_ff_4_q));  // open: nQ
  and and_14 (and_14_out, ~jk_ff_3_q, jk_ff_2_q, ~jk_ff_1_q);  // And
  and and_15 (and_15_out, jk_ff_3_q, ~jk_ff_2_q, ~jk_ff_1_q);  // And
  or or_4 (or_4_out, and_16_out, and_15_out, and_14_out, and_13_out);
  and and_16 (and_16_out, jk_ff_1_q, jk_ff_2_q, jk_ff_3_q);
endmodule
